# Fritzing sketch matriz (saved by Fritzing 1.0.2b)
breadboards: 1

parts:
  Componente1 = Arduino Mega 2560 (Rev3)
  D1 = Diode [package=diode-hv]
  D2 = Diode [package=diode-hv]
  D3 = Diode [package=diode-hv]
  D4 = Diode [package=diode-hv]
  RE1 = KY-040 Rotary encoder [package=THT]
  U3 = WS2812 RGB LED matrix 1x8
  LCD1 = elegoo-2.8in-tft-display  # not connected

nets:
  N1: Componente1.D21/SCL, RE1.CLK
  N2: Componente1.D20/SDA, RE1.DT
  N3: Componente1.D19/RX1, RE1.SW
  N4: Componente1.D18/TX1, U3.DIN
  VCC: Componente1.5V, RE1.Vcc, U3.VCC
  N5: Componente1.D47, D1.C, D4.C
  N6: Componente1.D49, D2.C, D3.C
  GND: Componente1.GND, RE1.GND, U3.GND

custom parts:
  KY-040 Rotary encoder: KY-040 Rotary Encoder with switch on breakout borad from AZ Delivery
  WS2812 RGB LED matrix 1x8: WS2812 matrix 1x8
  elegoo-2.8in-tft-display: 2.8 Inch TFT LCD Touch Screen with SD Card Socket. 240*320 pixels RGB. 4 chip white LED backlight.
